// Logisim project Contador completo.circ as structural Verilog: 1 circuit, main circuit main
module main (
  input  [1:0] in_1
);

  wire and_1_out, and_2_out, and_3_out, and_4_out, and_5_out, and_6_out, button_1_out, demultiplexer_1_out0,
       demultiplexer_1_out1, demultiplexer_1_out2, demultiplexer_1_out3, demultiplexer_2_out0,
       demultiplexer_2_out1, demultiplexer_2_out2, demultiplexer_2_out3, demultiplexer_3_out0,
       demultiplexer_3_out1, demultiplexer_3_out2, demultiplexer_3_out3, j_k_ff_1_q, j_k_ff_2_q, j_k_ff_3_q,
       j_k_ff_4_q, multiplexer_1_out, multiplexer_2_out, multiplexer_3_out, not_1_out, not_2_out, or_1_out,
       or_2_out, xnor_1_out;

  and and_1 (and_1_out, demultiplexer_1_out0, demultiplexer_2_out0);
  not not_1 (not_1_out, demultiplexer_1_out2);
  Demultiplexer #(.select(2), .enable("false")) demultiplexer_1 (
    .out0(demultiplexer_1_out0), .out1(demultiplexer_1_out1), .out2(demultiplexer_1_out2),
    .out3(demultiplexer_1_out3), .in(j_k_ff_1_q), .sel(in_1));
  Button button_1 (.out(button_1_out));
  xnor xnor_1 (xnor_1_out, in_1[1], in_1[0]);
  and and_2 (and_2_out, demultiplexer_1_out0, demultiplexer_2_out0, demultiplexer_3_out0);
  or or_1 (or_1_out, ~in_1[1], xnor_1_out);  // OR_Gate
  or or_2 (or_2_out, xnor_1_out, ~in_1[0]);  // OR_Gate
  not not_2 (not_2_out, demultiplexer_1_out3);
  and and_3 (and_3_out, ~demultiplexer_2_out3, ~demultiplexer_1_out3);  // AND_Gate
  and and_4 (and_4_out, demultiplexer_3_out1, demultiplexer_2_out1);
  Demultiplexer #(.select(2), .enable("false")) demultiplexer_2 (
    .out0(demultiplexer_2_out0), .out1(demultiplexer_2_out1), .out2(demultiplexer_2_out2),
    .out3(demultiplexer_2_out3), .in(j_k_ff_2_q), .sel(in_1));
  Multiplexer #(.select(2), .enable("false")) multiplexer_1 (
    .in0(demultiplexer_1_out0), .in1(demultiplexer_1_out1), .in2(not_1_out), .in3(not_2_out),
    .out(multiplexer_1_out), .sel(in_1));
  J_K_Flip_Flop j_k_ff_1 (
    .J(or_1_out), .clk(button_1_out), .K(or_2_out), .Q(j_k_ff_1_q), .en(1'b1));  // open: Qn, preset, reset
  and and_5 (and_5_out, ~demultiplexer_1_out3, ~demultiplexer_2_out3, ~demultiplexer_3_out3);  // AND_Gate
  J_K_Flip_Flop j_k_ff_2 (
    .J(multiplexer_1_out), .clk(button_1_out), .K(multiplexer_1_out), .Q(j_k_ff_2_q), .en(1'b1));  // open: Qn, preset, reset
  Multiplexer #(.select(2), .enable("false")) multiplexer_2 (
    .in0(and_1_out), .in1(demultiplexer_2_out1), .in2(demultiplexer_2_out2), .in3(and_3_out),
    .out(multiplexer_2_out), .sel(in_1));
  J_K_Flip_Flop j_k_ff_3 (
    .J(multiplexer_2_out), .clk(button_1_out), .K(multiplexer_2_out), .Q(j_k_ff_3_q), .en(1'b1));  // open: Qn, preset, reset
  and and_6 (and_6_out, demultiplexer_3_out2, demultiplexer_2_out2);
  Demultiplexer #(.select(2), .enable("false")) demultiplexer_3 (
    .out0(demultiplexer_3_out0), .out1(demultiplexer_3_out1), .out2(demultiplexer_3_out2),
    .out3(demultiplexer_3_out3), .in(j_k_ff_3_q), .sel(in_1));
  J_K_Flip_Flop j_k_ff_4 (
    .J(multiplexer_3_out), .clk(button_1_out), .K(multiplexer_3_out), .Q(j_k_ff_4_q), .en(1'b1));  // open: Qn, preset, reset
  Multiplexer #(.select(2), .enable("false")) multiplexer_3 (
    .in0(and_2_out), .in1(and_4_out), .in2(and_6_out), .in3(and_5_out), .out(multiplexer_3_out), .sel(in_1));
  LED led_1 (.in(j_k_ff_4_q));
  LED led_2 (.in(j_k_ff_3_q));
  LED led_3 (.in(j_k_ff_1_q));
  LED led_4 (.in(j_k_ff_2_q));

  // Notes on the sheet:
  //   Contador Crescente
  //   Contador Decrescente
endmodule
